# Fritzing sketch ble_strip3 (saved by Fritzing 0.9.3b)
perfboards: 1

parts:
  R4 = Resistor [tolerance=±5% resistance=330 package="0805 [SMD]"]
  R6 = Resistor [tolerance=±5% resistance=330 package="0805 [SMD]"]
  J7 = female pin header, 3 pins [form="♀ (female)"]
  Part4 = Bluetooth HC-05 Macho
  J8 = female pin header, 2 pins [form="♀ (female)"]
  J9 = female pin header, 3 pins [form="♀ (female)"]
  Part1 = Arduino Pro Mini v13
  J10 = female pin header, 2 pins [form="♀ (female)"]
  C6 = Capacitor Polarized [package=panasonic_h13]
  C7 = Capacitor Polarized [package=panasonic_h13]

nets:
  N1: R4.Pin_0, Part1.D3_PWM
  N2: R4.Pin_1, J9.pin2
  N3: R6.Pin_0, Part1.D2
  N4: R6.Pin_1, J7.pin2
  5V: J7.pin1, Part4.VCC, J8.pin1, Part1.RAW, C6.+
  GND: J7.pin3, Part4.GND, J8.pin2, J9.pin3, Part1.GND, J10.pin2, C6.-, C7.-
  N5: Part4.TXD, Part1.D11_PWM/MOSI
  N6: Part4.RXD, Part1.D10_PWM/SS
  3.3V: J9.pin1, J10.pin1, C7.+
