# Fritzing sketch ble_strip6_deprecated (saved by Fritzing 0.9.3b)
perfboards: 1

parts:
  R6 = Resistor [tolerance=±5% resistance=330 package="0805 [SMD]"]
  J7 = female pin header, 3 pins [form="♀ (female)"]
  Part4 = Bluetooth HC-05 Macho
  C6 = Capacitor Polarized [package=panasonic_h13]
  J9 = Screw terminal - 2 pins [package=THT]
  J10 = female pin header, 3 pins [form="♀ (female)"]
  Part1 = Arduino Pro Mini v13

nets:
  N1: R6.Pin_0, Part1.D2
  N2: R6.Pin_1, J7.pin2
  5V: J7.pin1, Part4.VCC, C6.+, J9.pin2, J10.pin1, Part1.RAW
  GND: J7.pin3, Part4.GND, C6.-, J9.pin1, J10.pin3, Part1.GND
  N3: Part4.TXD, Part1.D11_PWM/MOSI
  N4: Part4.RXD, Part1.D10_PWM/SS
